// Logisim project alu.circ as structural Verilog: 7 circuits, main circuit main
module main (
  input  [31:0] X,
  input  [31:0] Y,
  input  [5:0] Switch__S,
  output Signed_Overflow,
  output [31:0] RESULT,
  output Equal
);

  wire AddOverflow, comparator_1_lt, comparator_2_eq, comparator_4_lt, SubOverflow;
  wire [15:0] invert16_1_out, invert16_2_out;
  wire [31:0] ADD, ADDU, AND, BITPAL, negator_1_out, OR, SLL, SLT, SLTU, SRA, SRL, SUB, SUBU;
  wire [31:31] LFSR;

  Shifter #(.width(32)) shifter_1 (.in(X), .\dist (Y[4:0]), .out(SLL));
  Adder #(.width(32)) adder_1 (.a(X), .b(Y), .out(ADD), .cout(AddOverflow));  // open: cin
  Subtractor #(.width(32)) subtractor_1 (.a(X), .b(Y), .out(SUBU));  // open: bin, bout
  Comparator #(.width(32)) comparator_1 (.a(X), .b(Y), .lt(comparator_1_lt));  // open: gt, eq
  invert16 invert16_1 (.in_1(X[15:0]), .out(invert16_1_out));
  invert16 invert16_2 (.in_1(X[31:16]), .out(invert16_2_out));
  assign SLT = {{31{1'b0}}, comparator_1_lt};  // Bit_Extender bit_extender_1
  Comparator #(.width(16)) comparator_2 (.a(invert16_1_out), .b(invert16_2_out), .eq(comparator_2_eq));  // open: gt, lt
  assign BITPAL = {{31{1'b0}}, comparator_2_eq};  // Bit_Extender bit_extender_2
  Multiplexer #(.select(5), .width(32), .enable("false")) multiplexer_1 (
    .in0(SLL), .in2(SRL), .in3(SRA), .in16(ADD), .in17(ADDU), .in18(SUB), .in19(SUBU), .in20(AND), .in21(OR),
    .in26(SLT), .in27(SLTU), .in30(BITPAL), .in31({LFSR[31], X[30:0]}), .out(RESULT),
    .sel({Switch__S[5], Switch__S[3:0]}));  // open: in1, in4, in5, in6, in7, in8, in9, in10, in11, in12, in13, in14, in15, in22, in23, in24, in25, in28, in29
  Shifter #(.width(32), .shift("lr")) shifter_2 (.in(X), .\dist (Y[4:0]), .out(SRL));
  Adder #(.width(32)) adder_2 (.a(X), .b(Y), .out(ADDU));  // open: cin, cout
  assign AND = X & Y;  // AND_Gate and_1, 32 bits wide
  overflow_detect overflow_detect_1 (
    .switch({Switch__S[5], Switch__S[3:0]}), .add_overflow(AddOverflow), .sub_overflow(SubOverflow),
    .out(Signed_Overflow));
  Comparator #(.width(32)) comparator_3 (.a(X), .b(Y), .eq(Equal));  // open: gt, lt
  Shifter #(.width(32), .shift("ar")) shifter_3 (.in(X), .\dist (Y[4:0]), .out(SRA));
  Adder #(.width(32)) adder_3 (.a(X), .b(negator_1_out), .out(SUB), .cout(SubOverflow));  // open: cin
  Negator #(.width(32)) negator_1 (.in(Y), .out(negator_1_out));
  Comparator #(.width(32), .mode("unsigned")) comparator_4 (.a(X), .b(Y), .lt(comparator_4_lt));  // open: gt, eq
  lfsr lfsr_1 (.in_1(X), .out(LFSR[31]));
  assign OR = X | Y;  // OR_Gate or_1, 32 bits wide
  assign SLTU = {{31{1'b0}}, comparator_4_lt};  // Bit_Extender bit_extender_3

  // Other names for the same wires on the sheet: Input_X[31:0] = X; Input_Y[31:0] = Y; LFSR[30:0] = X[30:0];
  //   Switch[4:0] = {Switch__S[5], Switch__S[3:0]}

  // Notes on the sheet:
  //   INPUTS to your circuit
  //   INPUT to your circuit
  //   SLL
  //   ADD
  //   SUBU
  //   SLT
  //   BITPAL
  //   SRL
  //   ADDU
  //   AND
  //   DON'T CHANGE THE INPUTS AND OUTPUTS! IF YOU DO SO, YOU NEED TO MAKE SURE THE PINS ARE IN THE RIGHT PLACES!
  //   OUTPUTS of your circuit
  //   SRA
  //   SUB
  //   OR
  //   SLTU
  //   LFSR
endmodule

module invert16 (
  input  [15:0] in_1,
  output [15:0] out
);

  invert8 invert8_1 (.in_1(in_1[7:0]), .out(out[15:8]));
  invert8 invert8_2 (.in_1(in_1[15:8]), .out(out[7:0]));
endmodule

module invert8 (
  input  [7:0] in_1,
  output [7:0] out
);

  invert4 invert4_1 (.in_1(in_1[3:0]), .out(out[7:4]));
  invert4 invert4_2 (.in_1(in_1[7:4]), .out(out[3:0]));
endmodule

module invert4 (
  input  [3:0] in_1,
  output [3:0] out
);

  invert2 invert2_1 (.in_1(in_1[1:0]), .out(out[3:2]));
  invert2 invert2_2 (.in_1(in_1[3:2]), .out(out[1:0]));
endmodule

module invert2 (
  input  [1:0] in_1,
  output [1:0] out
);


  assign out = {in_1[0], in_1[1]};
endmodule

module lfsr (
  input  [31:0] in_1,
  output out
);

  ExactlyOne xor_1 (.out(out), .in0(in_1[0]), .in1(in_1[2]), .in2(in_1[3]), .in3(in_1[5]));
endmodule

module overflow_detect (
  input  [4:0] switch,
  input  add_overflow,
  input  sub_overflow,
  output out
);

  wire and_1_out, and_2_out, comparator_1_eq, comparator_2_eq;

  Comparator #(.width(5)) comparator_1 (.a(switch), .b(5'b10000), .eq(comparator_1_eq));  // open: gt, lt
  Comparator #(.width(5)) comparator_2 (.a(switch), .b(5'b10011), .eq(comparator_2_eq));  // open: gt, lt
  and and_1 (and_1_out, comparator_1_eq, add_overflow);
  and and_2 (and_2_out, comparator_2_eq, sub_overflow);
  or or_1 (out, and_1_out, and_2_out);
endmodule
