// Logisim project cpu.circ as structural Verilog: 2 circuits, main circuit main
module main (
  input  [31:0] RS_READ_VALUE,
  input  [31:0] RT_READ_VALUE,
  input  [31:0] INSTRUCTION,
  input  CLOCK,
  input  RESET,
  output [31:0] t0,
  output [31:0] t1,
  output [31:0] t2,
  output [31:0] t3,
  output [4:0] RS,
  output [4:0] RT,
  output [4:0] Write_Register,
  output [31:0] RD_WRITE_VALUE,
  output RD_WRITE_ENABLE,
  output [23:0] FETCH_ADDRESS
);

  wire Access_Byte, ALU_signed_overflow, ALUSrc, and_1_out, and_3_out, and_4_out, and_5_out, and_6_out,
       and_9_out, and_10_out, and_11_out, and_12_out, and_13_out, and_14_out, and_15_out, and_16_out,
       and_18_out, BranchTake, comparator_1_eq, comparator_2_eq, comparator_3_eq, comparator_4_eq,
       comparator_5_eq, comparator_6_eq, Equal, IMD_TYPE, JAL, JR, Jump, LUI, Mem_Data_Type, MemToReg,
       MemWrite, OP0, OP1, OP2, OP3, op4, OP5, or_2_out, or_3_out, or_9_out, PCSrc, ReadInSubRegfile1,
       ReadInSubRegfile2, RegDst, SHIFT, WriteInSubRegfile;
  wire [1:0] sub_regfile_1_regnumber_2, sub_regfile_2_regnumber_2, sub_regfile_3_regnumber_2;
  wire [2:0] ALUOp;
  wire [4:0] multiplexer_3_out, SHAMT;
  wire [5:0] FuncField, Switch;
  wire [15:11] multiplexer_2_out;
  wire [23:0] adder_1_out, adder_2_out, adder_3_out, bit_extender_1_out, JumpAddr, multiplexer_9_out,
       multiplexer_12_out, NEXT_PC, PC_1, PC_q;
  wire [31:0] ALU_result, bit_extender_2_out, bit_extender_3_out, bit_extender_4_out, bit_extender_5_out,
       bit_extender_6_out, bit_extender_7_out, IMD, main_1_read_data_1, main_1_read_data_2, MEM_data_mem_out,
       multiplexer_8_out, multiplexer_10_out, multiplexer_11_out, multiplexer_13_out, multiplexer_14_out,
       multiplexer_16_out, multiplexer_17_out, multiplexer_18_out, register_1_q, RS_Value, RT_Value;

  Multiplexer #(.width(24), .enable("false")) multiplexer_1 (
    .in0(PC_q), .in1(NEXT_PC), .out(FETCH_ADDRESS), .sel(PCSrc));
  Adder #(.width(24)) adder_1 (.a(FETCH_ADDRESS), .b(24'h1), .out(adder_1_out));  // open: cin, cout
  sub_regfile sub_regfile_1 (
    .RegNumber(RS), .Is_sub_regfile(ReadInSubRegfile1), .RegNumber_2(sub_regfile_1_regnumber_2));
  sub_regfile sub_regfile_2 (
    .RegNumber(RT), .Is_sub_regfile(ReadInSubRegfile2), .RegNumber_2(sub_regfile_2_regnumber_2));
  sub_regfile sub_regfile_3 (
    .RegNumber(Write_Register), .Is_sub_regfile(WriteInSubRegfile), .RegNumber_2(sub_regfile_3_regnumber_2));
  Register #(.width(24)) PC (.D(adder_1_out), .Q(PC_q), .clk(CLOCK));  // open: en, clr
  Register #(.width(24)) u_PC_1 (.D(adder_1_out), .Q(PC_1), .clk(CLOCK));  // open: en, clr
  Register #(.width(32)) register_1 (.D(INSTRUCTION), .Q(register_1_q), .clk(CLOCK));  // open: en, clr
  Multiplexer #(.width(32), .enable("false")) multiplexer_2 (
    .in0(register_1_q), .in1({32{1'b0}}),
    .out({OP5, op4, OP3, OP2, OP1, OP0, RS, RT, multiplexer_2_out, SHAMT, FuncField}), .sel(PCSrc));
  and and_1 (and_1_out, WriteInSubRegfile, RD_WRITE_ENABLE);
  Multiplexer #(.width(5), .enable("false")) multiplexer_3 (
    .in0(RT), .in1(multiplexer_2_out), .out(multiplexer_3_out), .sel(RegDst));
  regfile_main main_1 (
    .Read_register_1(sub_regfile_1_regnumber_2), .Read_register_2(sub_regfile_2_regnumber_2),
    .write_register(sub_regfile_3_regnumber_2), .write_data(RD_WRITE_VALUE), .t0_Value(t0), .t1_Value(t1),
    .t2_Value(t2), .t3_Value(t3), .RegWrite(and_1_out), .clock(CLOCK), .Read_Data_1(main_1_read_data_1),
    .Read_Data_2(main_1_read_data_2));
  Multiplexer #(.width(5), .enable("false")) multiplexer_4 (
    .in0(multiplexer_3_out), .in1({5{1'b1}}), .out(Write_Register), .sel(JAL));
  assign bit_extender_1_out = {{8{multiplexer_2_out[15]}}, {multiplexer_2_out, SHAMT, FuncField}};  // Bit_Extender bit_extender_1
  assign bit_extender_2_out = {{16{multiplexer_2_out[15]}}, {multiplexer_2_out, SHAMT, FuncField}};  // Bit_Extender bit_extender_2
  assign bit_extender_3_out = {{16{1'b0}}, {multiplexer_2_out, SHAMT, FuncField}};  // Bit_Extender bit_extender_3
  Comparator #(.width(6), .mode("unsigned")) comparator_1 (
    .a(FuncField), .b(6'b001000), .eq(comparator_1_eq));  // open: gt, lt
  Comparator #(.width(6)) comparator_2 (
    .a({6{1'b0}}), .b({OP5, op4, OP3, OP2, OP1, OP0}), .eq(comparator_2_eq));  // open: gt, lt
  Adder #(.width(24)) adder_2 (.a(PC_1), .b(bit_extender_1_out), .out(adder_2_out));  // open: cin, cout
  Multiplexer #(.width(32), .enable("false")) multiplexer_5 (
    .in0(bit_extender_2_out), .in1(bit_extender_3_out), .out(IMD), .sel(IMD_TYPE));
  Multiplexer #(.width(32), .enable("false")) multiplexer_6 (
    .in0(RS_READ_VALUE), .in1(main_1_read_data_1), .out(RS_Value), .sel(ReadInSubRegfile1));
  Multiplexer #(.width(32), .enable("false")) multiplexer_7 (
    .in0(RT_READ_VALUE), .in1(main_1_read_data_2), .out(RT_Value), .sel(ReadInSubRegfile2));
  and and_2 (JR, comparator_1_eq, comparator_2_eq);
  Multiplexer #(.width(32), .enable("false")) multiplexer_8 (
    .in0(RT_Value), .in1(IMD), .out(multiplexer_8_out), .sel(ALUSrc));
  Multiplexer #(.width(24), .enable("false")) multiplexer_9 (
    .in0({RS[2:0], RT, multiplexer_2_out, SHAMT, FuncField}), .in1(RS_Value[23:0]), .out(multiplexer_9_out),
    .sel(JR));
  Subtractor #(.width(24)) subtractor_1 (.a(multiplexer_9_out), .b(24'h100000), .out(JumpAddr));  // open: bin, bout
  Multiplexer #(.width(32), .enable("false")) multiplexer_10 (
    .in0(RS_Value), .in1(IMD), .out(multiplexer_10_out), .sel(LUI));
  Multiplexer #(.width(32), .enable("false")) multiplexer_11 (
    .in0(multiplexer_8_out), .in1(32'h10), .out(multiplexer_11_out), .sel(LUI));
  assign bit_extender_4_out = {{27{1'b0}}, SHAMT};  // Bit_Extender bit_extender_4
  Comparator #(.width(6), .mode("unsigned")) comparator_3 (
    .a(FuncField), .b({6{1'b0}}), .eq(comparator_3_eq));  // open: gt, lt
  Comparator #(.width(6), .mode("unsigned")) comparator_4 (
    .a(FuncField), .b(6'b000010), .eq(comparator_4_eq));  // open: gt, lt
  Comparator #(.width(6), .mode("unsigned")) comparator_5 (
    .a(FuncField), .b(6'b000011), .eq(comparator_5_eq));  // open: gt, lt
  and and_3 (and_3_out, ~OP0, ~OP1, ~OP2, ~OP3, ~op4, ~OP5);  // AND_Gate
  and and_4 (and_4_out, OP3, ~op4, ~OP5);  // AND_Gate
  and and_5 (and_5_out, ~OP3, ~op4, OP5);  // AND_Gate
  and and_6 (and_6_out, OP0, OP1, ~OP2, ~OP3, ~op4, ~OP5);  // AND_Gate
  or or_1 (ALUSrc, OP3, OP5);
  and and_7 (MemToReg, ~OP3, OP5);  // AND_Gate
  and and_8 (MemWrite, OP3, OP5);
  and and_9 (and_9_out, OP2, ~OP3, ~op4, ~OP5);  // AND_Gate
  and and_10 (and_10_out, OP0, ~Equal);  // AND_Gate
  and and_11 (and_11_out, ~OP0, Equal);  // AND_Gate
  and and_12 (and_12_out, OP0, ~OP1, ~OP2);  // AND_Gate
  and and_13 (and_13_out, OP0, ~OP1, OP2, OP3);  // AND_Gate
  and and_14 (and_14_out, ~OP0, ~OP1, ~OP2, ~OP3, ~op4, ~OP5);  // AND_Gate
  and and_15 (and_15_out, ~OP1, OP2, OP3);  // AND_Gate
  and and_16 (and_16_out, OP0, OP1, OP2, OP3);
  and and_17 (LUI, OP0, OP1, OP2, OP3);
  and and_18 (and_18_out, OP1, ~OP2, ~OP3, ~op4, ~OP5);  // AND_Gate
  and and_19 (JAL, OP0, OP1, ~OP2, ~OP3, ~op4, ~OP5);  // AND_Gate
  and and_20 (Mem_Data_Type, ~OP0, ~OP1, OP2, ~OP3, ~op4, OP5);  // AND_Gate
  and and_21 (IMD_TYPE, OP0, ~OP1, OP2, OP3);  // AND_Gate
  and and_22 (Access_Byte, ~OP0, ~OP1, ~OP3, ~op4, OP5);  // AND_Gate
  Multiplexer #(.width(24), .enable("false")) multiplexer_12 (
    .in0(adder_2_out), .in1(JumpAddr), .out(multiplexer_12_out), .sel(Jump));
  Multiplexer #(.width(32), .enable("false")) multiplexer_13 (
    .in0(multiplexer_11_out), .in1(bit_extender_4_out), .out(multiplexer_13_out), .sel(SHIFT));
  or or_2 (or_2_out, and_10_out, and_11_out);
  Multiplexer #(.width(32), .enable("false")) multiplexer_14 (
    .in0(multiplexer_10_out), .in1(RT_Value), .out(multiplexer_14_out), .sel(SHIFT));
  or or_3 (or_3_out, comparator_3_eq, comparator_4_eq, comparator_5_eq);
  Comparator #(.width(6)) comparator_6 (
    .a({6{1'b0}}), .b({OP5, op4, OP3, OP2, OP1, OP0}), .eq(comparator_6_eq));  // open: gt, lt
  and and_23 (RegDst, ~OP0, ~OP1, ~OP2, ~OP3, ~op4, ~OP5);  // AND_Gate
  or or_4 (RD_WRITE_ENABLE, and_3_out, and_4_out, and_5_out, and_6_out);
  and and_24 (BranchTake, and_9_out, or_2_out);
  or or_5 (ALUOp[0], and_12_out, and_13_out, and_14_out);
  or or_6 (ALUOp[1], and_14_out, and_15_out);
  or or_7 (ALUOp[2], and_14_out, and_16_out);
  LED led_1 (.in(ALU_signed_overflow));
  alu_main ALU (
    .Switch__S(Switch), .X(multiplexer_14_out), .Equal(Equal), .RESULT(ALU_result),
    .Signed_Overflow(ALU_signed_overflow), .Y(multiplexer_13_out));
  Multiplexer #(.select(3), .width(6), .enable("false")) multiplexer_15 (
    .in0(6'b100000), .in1(6'b100001), .in2(6'b100100), .in3(6'b100101), .in4({6{1'b0}}), .in5(6'b100010),
    .in7(FuncField), .out(Switch), .sel(ALUOp));  // open: in6
  and and_25 (SHIFT, or_3_out, comparator_6_eq);
  or or_8 (Jump, and_18_out, JR);
  mem_main MEM (
    .Data_Mem_Addr(ALU_result), .Data_Mem_In(RT_Value), .ACCESS_BYTE(Access_Byte), .MEM_WRITE(MemWrite),
    .CLOCK(CLOCK), .Data_Mem_Out(MEM_data_mem_out));
  assign bit_extender_5_out = {{24{MEM_data_mem_out[7]}}, MEM_data_mem_out[7:0]};  // Bit_Extender bit_extender_5
  assign bit_extender_6_out = {{24{1'b0}}, MEM_data_mem_out[7:0]};  // Bit_Extender bit_extender_6
  or or_9 (or_9_out, BranchTake, Jump);
  Multiplexer #(.width(32), .enable("false")) multiplexer_16 (
    .in0(MEM_data_mem_out), .in1(multiplexer_17_out), .out(multiplexer_16_out), .sel(Access_Byte));
  Multiplexer #(.width(32), .enable("false")) multiplexer_17 (
    .in0(bit_extender_5_out), .in1(bit_extender_6_out), .out(multiplexer_17_out), .sel(Mem_Data_Type));
  Register #(.width(24)) register_2 (.D(multiplexer_12_out), .Q(NEXT_PC), .clk(CLOCK));  // open: en, clr
  Register #(.width(1)) register_3 (.D(or_9_out), .Q(PCSrc), .clk(CLOCK));  // open: en, clr
  Multiplexer #(.width(32), .enable("false")) multiplexer_18 (
    .in0(ALU_result), .in1(multiplexer_16_out), .out(multiplexer_18_out), .sel(MemToReg));
  Multiplexer #(.width(32), .enable("false")) multiplexer_19 (
    .in0(multiplexer_18_out), .in1(bit_extender_7_out), .out(RD_WRITE_VALUE), .sel(JAL));
  Adder #(.width(24)) adder_3 (.a(PC_1), .b(24'h100000), .out(adder_3_out));  // open: cin, cout
  assign bit_extender_7_out = {{8{1'b0}}, adder_3_out};  // Bit_Extender bit_extender_7

  // Other names for the same wires on the sheet: ReadReg2[4:0] = RT; ReadReg1[4:0] = RS;
  //   OPCode[5:0] = {OP5, op4, OP3, OP2, OP1, OP0}; Instruction_Addr[23:0] = FETCH_ADDRESS;
  //   RegWrite = RD_WRITE_ENABLE; RS_Main_Value[31:0] = RS_READ_VALUE; RT_Main_Value[31:0] = RT_READ_VALUE;
  //   WRITE_DATA[31:0] = RD_WRITE_VALUE; WriteReg[4:0] = Write_Register

  // Notes on the sheet:
  //   These are outputs/inputs from run.circ
  //   PC+1
  //   Register Select Circuit
  //   These are outputs to run.circ
  //   Controll Unit
  //   Branch Type
  //   Branch Target
  //   CPU
  //   Is Branch
  //   ALU Control
endmodule

module sub_regfile (
  input  [4:0] RegNumber,
  output Is_sub_regfile,
  output [1:0] RegNumber_2
);

  wire comparator_1_lt, comparator_2_gt;
  wire [4:2] subtractor_1_out;

  Comparator #(.width(5)) comparator_1 (.a(RegNumber), .b(5'b01000), .lt(comparator_1_lt));  // open: gt, eq
  Comparator #(.width(5)) comparator_2 (.a(RegNumber), .b(5'b01011), .gt(comparator_2_gt));  // open: eq, lt
  Subtractor #(.width(5)) subtractor_1 (
    .a(RegNumber), .b(5'b01000), .out({subtractor_1_out, RegNumber_2}));  // open: bin, bout
  nor nor_1 (Is_sub_regfile, comparator_1_lt, comparator_2_gt);
endmodule
