// Logisim project mem.circ as structural Verilog: 1 circuit, main circuit main
module main (
  input  [31:0] Data_Mem_Addr,
  input  [31:0] Data_Mem_In,
  input  ACCESS_BYTE,
  input  MEM_WRITE,
  input  CLOCK,
  output [31:0] Data_Mem_Out
);

  wire and_1_out, not_1_out;
  wire [7:0] multiplexer_1_out;
  wire [23:0] subtractor_1_out;
  wire [31:0] bit_extender_1_out, ram_1_data;

  Subtractor #(.width(24)) subtractor_1 (
    .a(Data_Mem_Addr[25:2]), .b(24'h4000), .out(subtractor_1_out));  // open: bin, bout
  RAM #(.addrWidth(24), .dataWidth(32)) ram_1 (
    .addr(subtractor_1_out), .data(ram_1_data), .sel(1'b1), .clk(CLOCK), .ld(not_1_out), .clr(1'b0));
  not not_1 (not_1_out, MEM_WRITE);
  assign ram_1_data = MEM_WRITE ? Data_Mem_In : 32'bz;  // Controlled_Buffer controlled_buffer_1
  Multiplexer #(.select(2), .width(8), .enable("false")) multiplexer_1 (
    .in0(ram_1_data[7:0]), .in1(ram_1_data[15:8]), .in2(ram_1_data[23:16]), .in3(ram_1_data[31:24]),
    .out(multiplexer_1_out), .sel(Data_Mem_Addr[1:0]));
  assign bit_extender_1_out = {{24{1'b0}}, multiplexer_1_out};  // Bit_Extender bit_extender_1
  Multiplexer #(.width(32), .enable("false")) multiplexer_2 (
    .in0(ram_1_data), .in1(bit_extender_1_out), .out(Data_Mem_Out), .sel(and_1_out));
  and and_1 (and_1_out, ACCESS_BYTE, ~MEM_WRITE);  // AND_Gate

  // Other names for the same wires on the sheet: ByteOffset[1:0] = Data_Mem_Addr[1:0]

  // Notes on the sheet:
  //   These are INPUTS to the circuit
  //   These are INPUTS to the circuit
  //   DO NOT CHANGE THE LOCATIONS OF THE INPUTS/OUTPUTS! IF YOU DO SO, YOU NEED TO MAKE SURE THE PINS ARE AT THE RIGHT PLACE!
  //   Yet again, the clock is not an actual clock, but an input, one that will be driven from a higher circuit
  //   This is an OUTPUT to the circuit
endmodule
